// Logisim project Lab6 - Copy.circ as structural Verilog: 33 circuits, main circuit main
module main (
);

  wire clock_1_out, comparator_1_eq, comparator_2_eq, comparator_3_eq, controlled_buffer_1_out,
       execute_1_cnd, fetch_1_invalid_instr, memory_1_dmem_error, register_1_q, stat_1_out_6;
  wire [3:0] fetch_1_code, fetch_1_ifun, fetch_1_ra, fetch_1_rb, icodreg_q, ifunreg_q, ra_q, rb_q;
  wire [7:0] counter_1_q;
  wire [63:0] decode_1_vala, decode_1_valb, execute_1_vale, fetch_1_valc, fetch_1_valp, memory_1_valm,
       pcupdate_1_pc, valA_q, valB_q, valcreg_q, vale_q, valpreg_q;

  Clock clock_1 (.out(clock_1_out));
  assign controlled_buffer_1_out = stat_1_out_6 ? clock_1_out : 1'bz;  // Controlled_Buffer controlled_buffer_1
  stat stat_1 (
    .halt(icodreg_q), .imem(fetch_1_invalid_instr), .instr_valid(fetch_1_invalid_instr),
    .dmem(memory_1_dmem_error), .clk(controlled_buffer_1_out), .out_6(stat_1_out_6));
  Fetch fetch_1 (
    .PC(pcupdate_1_pc), .clk(controlled_buffer_1_out), .rA(fetch_1_ra), .rB(fetch_1_rb), .valC(fetch_1_valc),
    .valP(fetch_1_valp), .code(fetch_1_code), .ifun(fetch_1_ifun), .invalid_instr(fetch_1_invalid_instr),
    .imem_error(fetch_1_invalid_instr));
  Counter_part #(.max('h1a)) counter_1 (
    .clk(controlled_buffer_1_out), .Q(counter_1_q));  // open: clr, load, up, count, D, carry
  Register #(.width(4)) ra (
    .D(fetch_1_ra), .en(comparator_1_eq), .clk(controlled_buffer_1_out), .Q(ra_q));  // open: clr
  Register #(.width(4)) rb (
    .D(fetch_1_rb), .en(comparator_1_eq), .clk(controlled_buffer_1_out), .Q(rb_q));  // open: clr
  Register #(.width(64)) valcreg (
    .D(fetch_1_valc), .en(comparator_1_eq), .clk(controlled_buffer_1_out), .Q(valcreg_q));  // open: clr
  Register #(.width(64)) valpreg (
    .D(fetch_1_valp), .en(comparator_1_eq), .clk(controlled_buffer_1_out), .Q(valpreg_q));  // open: clr
  Register #(.width(4)) icodreg (
    .D(fetch_1_code), .en(comparator_1_eq), .clk(controlled_buffer_1_out), .Q(icodreg_q));  // open: clr
  Register #(.width(4)) ifunreg (
    .D(fetch_1_ifun), .en(comparator_1_eq), .clk(controlled_buffer_1_out), .Q(ifunreg_q));  // open: clr
  Comparator comparator_1 (.a(counter_1_q), .b(8'h9), .eq(comparator_1_eq));  // open: gt, lt
  Comparator comparator_2 (.a(counter_1_q), .b(8'hc), .eq(comparator_2_eq));  // open: gt, lt
  Register #(.width(64)) valA (
    .D(decode_1_vala), .en(comparator_2_eq), .clk(controlled_buffer_1_out), .Q(valA_q));  // open: clr
  Decode decode_1 (
    .rA(ra_q), .rB(rb_q), .icode(icodreg_q), .valM(memory_1_valm), .valE(vale_q),
    .clk(controlled_buffer_1_out), .ValA(decode_1_vala), .ValB(decode_1_valb));
  Register #(.width(64)) valB (
    .D(decode_1_valb), .en(comparator_2_eq), .clk(controlled_buffer_1_out), .Q(valB_q));  // open: clr
  Execute execute_1 (
    .valC(valcreg_q), .valA(valA_q), .icode(icodreg_q), .valB(valB_q), .ifun(ifunreg_q),
    .clk(controlled_buffer_1_out), .valE(execute_1_vale), .cnd(execute_1_cnd));
  Comparator comparator_3 (.a(counter_1_q), .b(8'hd), .eq(comparator_3_eq));  // open: gt, lt
  Register #(.width(64)) vale (
    .D(execute_1_vale), .en(comparator_3_eq), .clk(controlled_buffer_1_out), .Q(vale_q));  // open: clr
  Register #(.width(1)) register_1 (
    .D(execute_1_cnd), .en(comparator_3_eq), .clk(controlled_buffer_1_out), .Q(register_1_q));  // open: clr
  Memory memory_1 (
    .icode(icodreg_q), .valE(vale_q), .valA(valA_q), .valP(valpreg_q), .clk(controlled_buffer_1_out),
    .dmem_error(memory_1_dmem_error), .valM(memory_1_valm));
  PCUpdate pcupdate_1 (
    .icode(icodreg_q), .cnd(register_1_q), .valC(valcreg_q), .valM(memory_1_valm), .valP(valpreg_q),
    .clk(controlled_buffer_1_out), .PC(pcupdate_1_pc));

  // Notes on the sheet:
  //   0-9
  //   10
  //   11
  //   12
  //   13
endmodule

module Fetch (
  input  [63:0] PC,
  input  clk,
  output [3:0] rA,
  output [3:0] rB,
  output [63:0] valC,
  output [63:0] valP,
  output [3:0] code,
  output [3:0] ifun,
  output invalid_instr,
  output imem_error
);

  wire align_1_needregids, align_1_needvalc, both_out, comparator_1_eq, cOnly_out, not_1_out;
  wire [4:0] counter_1_q;
  wire [7:0] instructionmemory_1_b0, instructionmemory_1_b1, instructionmemory_1_b2, instructionmemory_1_b3,
       instructionmemory_1_b4, instructionmemory_1_b5, instructionmemory_1_b6, instructionmemory_1_b7,
       instructionmemory_1_b8, instructionmemory_1_b9;
  wire [63:0] controlled_buffer_5_out;

  Split split_1 (.in_1(instructionmemory_1_b0), .icode(code), .ifun(ifun), .invalid_instr(invalid_instr));
  InstructionMemory instructionmemory_1 (
    .PC(PC), .clk(clk), .b1(instructionmemory_1_b1), .b2(instructionmemory_1_b2),
    .b3(instructionmemory_1_b3), .b4(instructionmemory_1_b4), .b5(instructionmemory_1_b5),
    .b6(instructionmemory_1_b6), .b7(instructionmemory_1_b7), .b8(instructionmemory_1_b8),
    .b9(instructionmemory_1_b9), .b0(instructionmemory_1_b0), .imem_error(imem_error));
  Align align_1 (.code(code), .NeedRegids(align_1_needregids), .NeedValC(align_1_needvalc));  // open: ifun
  assign valC = both_out ? {instructionmemory_1_b9, instructionmemory_1_b8, instructionmemory_1_b7, instructionmemory_1_b6, instructionmemory_1_b5, instructionmemory_1_b4, instructionmemory_1_b3, instructionmemory_1_b2} : 64'bz;  // Controlled_Buffer controlled_buffer_1
  and both (both_out, align_1_needregids, align_1_needvalc);
  assign valC = cOnly_out ? {instructionmemory_1_b8, instructionmemory_1_b7, instructionmemory_1_b6, instructionmemory_1_b5, instructionmemory_1_b4, instructionmemory_1_b3, instructionmemory_1_b2, instructionmemory_1_b1} : 64'bz;  // Controlled_Buffer controlled_buffer_2
  and cOnly (cOnly_out, align_1_needvalc, ~align_1_needregids);  // AND_Gate
  assign {rA, rB} = align_1_needregids ? instructionmemory_1_b1 : 8'bz;  // Controlled_Buffer controlled_buffer_3
  assign {rA, rB} = not_1_out ? 8'hf : 8'bz;  // Controlled_Buffer controlled_buffer_4
  not not_1 (not_1_out, align_1_needregids);
  assign controlled_buffer_5_out = comparator_1_eq ? PC : 64'bz;  // Controlled_Buffer controlled_buffer_5
  PCIncrement pcincrement_1 (
    .PC(controlled_buffer_5_out), .needs_reg(align_1_needregids), .needs_valC(align_1_needvalc), .PC0(valP));
  Comparator #(.width(5)) comparator_1 (.a(5'b01001), .b(counter_1_q), .eq(comparator_1_eq));  // open: gt, lt
  Counter_part #(.max('h1a), .width(5)) counter_1 (.clk(clk), .Q(counter_1_q));  // open: clr, load, up, count, D, carry
endmodule

module Decode (
  input  [3:0] rA,
  input  [3:0] rB,
  input  [3:0] icode,
  input  [63:0] valM,
  input  [63:0] valE,
  input  clk,
  output [63:0] ValA,
  output [63:0] ValB
);

  wire comparator_1_eq, decmux_1_enable, decmux_2_enable, decmux_3_enable, decmux_4_enable, decmux_5_enable,
       decmux_6_enable, decmux_7_enable, decmux_8_enable, decmux_9_enable, decmux_10_enable,
       decmux_11_enable, decmux_12_enable, decmux_13_enable, decmux_14_enable, decmux_15_enable, ED_r0,
       ED_r1, ED_r2, ED_r3, ED_r4, ED_r5, ED_r6, ED_r7, ED_r8, ED_r9, ED_r10, ED_r11, ED_r12, ED_r13, ED_r14,
       MD_r0, MD_r1, MD_r2, MD_r3, MD_r4, MD_r5, MD_r6, MD_r7, MD_r8, MD_r9, MD_r10, MD_r11, MD_r12, MD_r13,
       MD_r14, or_1_out, or_2_out, or_3_out, or_4_out, or_5_out, or_6_out, or_7_out, or_8_out, or_9_out,
       or_10_out, or_11_out, or_12_out, or_13_out, or_14_out, or_15_out, srcA_decode_r0, srcA_decode_r1,
       srcA_decode_r2, srcA_decode_r3, srcA_decode_r4, srcA_decode_r5, srcA_decode_r6, srcA_decode_r7,
       srcA_decode_r8, srcA_decode_r9, srcA_decode_r10, srcA_decode_r11, srcA_decode_r12, srcA_decode_r13,
       srcA_decode_r14, srcB_decode_r0, srcB_decode_r1, srcB_decode_r2, srcB_decode_r3, srcB_decode_r4,
       srcB_decode_r5, srcB_decode_r6, srcB_decode_r7, srcB_decode_r8, srcB_decode_r9, srcB_decode_r10,
       srcB_decode_r11, srcB_decode_r12, srcB_decode_r13, srcB_decode_r14;
  wire [3:0] icodetoinputvals_1_dste, icodetoinputvals_1_dstm, icodetoinputvals_1_srca,
       icodetoinputvals_1_srcb;
  wire [4:0] counter_1_q;
  wire [63:0] multiplexer_1_out, multiplexer_2_out, multiplexer_3_out, multiplexer_4_out, multiplexer_5_out,
       multiplexer_6_out, multiplexer_7_out, multiplexer_8_out, multiplexer_9_out, multiplexer_10_out,
       multiplexer_11_out, multiplexer_12_out, multiplexer_13_out, multiplexer_14_out, multiplexer_15_out,
       r8_8_q, r9_q, r10_q, r11_q, r12_q, r13_q, r14_q, rax_0_q, rbp_5_q, rbx_3_q, rcx_1_q, rdi_7_q, rdx_2_q,
       rsi_6_q, rsp_4_q;

  addr_decode MD (
    .src(icodetoinputvals_1_dstm), .r0(MD_r0), .r1(MD_r1), .r2(MD_r2), .r3(MD_r3), .r4(MD_r4), .r5(MD_r5),
    .r6(MD_r6), .r7(MD_r7), .r8(MD_r8), .r9(MD_r9), .r10(MD_r10), .r11(MD_r11), .r12(MD_r12), .r13(MD_r13),
    .r14(MD_r14));
  addr_decode ED (
    .src(icodetoinputvals_1_dste), .r0(ED_r0), .r1(ED_r1), .r2(ED_r2), .r3(ED_r3), .r4(ED_r4), .r5(ED_r5),
    .r6(ED_r6), .r7(ED_r7), .r8(ED_r8), .r9(ED_r9), .r10(ED_r10), .r11(ED_r11), .r12(ED_r12), .r13(ED_r13),
    .r14(ED_r14));
  icodeToInputVals icodetoinputvals_1 (
    .rA(rA), .rB(rB), .rsp(4'b0100), .i0(icode[0]), .i1(icode[1]), .i2(icode[2]), .i3(icode[3]),
    .srcA(icodetoinputvals_1_srca), .srcB(icodetoinputvals_1_srcb), .dstE(icodetoinputvals_1_dste),
    .dstM(icodetoinputvals_1_dstm));
  Counter_part #(.max('h1a), .width(5)) counter_1 (.clk(clk), .Q(counter_1_q));  // open: clr, load, up, count, D, carry
  Comparator #(.width(5)) comparator_1 (.a(5'b11001), .b(counter_1_q), .eq(comparator_1_eq));  // open: gt, lt
  or or_1 (or_1_out, ED_r0, MD_r0);
  or or_2 (or_2_out, ED_r1, MD_r1);
  or or_3 (or_3_out, ED_r2, MD_r2);
  or or_4 (or_4_out, ED_r3, MD_r3);
  or or_5 (or_5_out, ED_r4, MD_r4);
  or or_6 (or_6_out, ED_r5, MD_r5);
  or or_7 (or_7_out, ED_r6, MD_r6);
  or or_8 (or_8_out, ED_r7, MD_r7);
  or or_9 (or_9_out, ED_r8, MD_r8);
  or or_10 (or_10_out, ED_r9, MD_r9);
  or or_11 (or_11_out, ED_r10, MD_r10);
  or or_12 (or_12_out, ED_r11, MD_r11);
  or or_13 (or_13_out, ED_r12, MD_r12);
  or or_14 (or_14_out, ED_r13, MD_r13);
  or or_15 (or_15_out, ED_r14, MD_r14);
  Multiplexer #(.width(64)) multiplexer_1 (.in0(valE), .in1(valM), .out(multiplexer_1_out), .sel(MD_r0));
  Multiplexer #(.width(64)) multiplexer_2 (.in0(valE), .in1(valM), .out(multiplexer_2_out), .sel(MD_r1));
  Multiplexer #(.width(64)) multiplexer_3 (.in0(valE), .in1(valM), .out(multiplexer_3_out), .sel(MD_r2));
  Multiplexer #(.width(64)) multiplexer_4 (.in0(valE), .in1(valM), .out(multiplexer_4_out), .sel(MD_r3));
  Multiplexer #(.width(64)) multiplexer_5 (.in0(valE), .in1(valM), .out(multiplexer_5_out), .sel(MD_r4));
  Multiplexer #(.width(64)) multiplexer_6 (.in0(valE), .in1(valM), .out(multiplexer_6_out), .sel(MD_r5));
  Multiplexer #(.width(64)) multiplexer_7 (.in0(valE), .in1(valM), .out(multiplexer_7_out), .sel(MD_r6));
  Multiplexer #(.width(64)) multiplexer_8 (.in0(valE), .in1(valM), .out(multiplexer_8_out), .sel(MD_r7));
  Multiplexer #(.width(64)) multiplexer_9 (.in0(valE), .in1(valM), .out(multiplexer_9_out), .sel(MD_r8));
  Multiplexer #(.width(64)) multiplexer_10 (.in0(valE), .in1(valM), .out(multiplexer_10_out), .sel(MD_r9));
  Multiplexer #(.width(64)) multiplexer_11 (.in0(valE), .in1(valM), .out(multiplexer_11_out), .sel(MD_r10));
  Multiplexer #(.width(64)) multiplexer_12 (.in0(valE), .in1(valM), .out(multiplexer_12_out), .sel(MD_r11));
  Multiplexer #(.width(64)) multiplexer_13 (.in0(valE), .in1(valM), .out(multiplexer_13_out), .sel(MD_r12));
  Multiplexer #(.width(64)) multiplexer_14 (.in0(valE), .in1(valM), .out(multiplexer_14_out), .sel(MD_r13));
  Multiplexer #(.width(64)) multiplexer_15 (.in0(valE), .in1(valM), .out(multiplexer_15_out), .sel(MD_r14));
  decmux decmux_1 (.wen(or_1_out), .counter(comparator_1_eq), .enable(decmux_1_enable));
  decmux decmux_2 (.wen(or_2_out), .counter(comparator_1_eq), .enable(decmux_2_enable));
  decmux decmux_3 (.wen(or_3_out), .counter(comparator_1_eq), .enable(decmux_3_enable));
  decmux decmux_4 (.wen(or_4_out), .counter(comparator_1_eq), .enable(decmux_4_enable));
  decmux decmux_5 (.wen(or_5_out), .counter(comparator_1_eq), .enable(decmux_5_enable));
  decmux decmux_6 (.wen(or_6_out), .counter(comparator_1_eq), .enable(decmux_6_enable));
  decmux decmux_7 (.wen(or_7_out), .counter(comparator_1_eq), .enable(decmux_7_enable));
  decmux decmux_8 (.wen(or_8_out), .counter(comparator_1_eq), .enable(decmux_8_enable));
  decmux decmux_9 (.wen(or_9_out), .counter(comparator_1_eq), .enable(decmux_9_enable));
  decmux decmux_10 (.wen(or_10_out), .counter(comparator_1_eq), .enable(decmux_10_enable));
  decmux decmux_11 (.wen(or_11_out), .counter(comparator_1_eq), .enable(decmux_11_enable));
  decmux decmux_12 (.wen(or_12_out), .counter(comparator_1_eq), .enable(decmux_12_enable));
  decmux decmux_13 (.wen(or_13_out), .counter(comparator_1_eq), .enable(decmux_13_enable));
  decmux decmux_14 (.wen(or_14_out), .counter(comparator_1_eq), .enable(decmux_14_enable));
  decmux decmux_15 (.wen(or_15_out), .counter(comparator_1_eq), .enable(decmux_15_enable));
  Register #(.width(64)) rax_0 (.D(multiplexer_1_out), .en(decmux_1_enable), .clk(clk), .Q(rax_0_q));  // open: clr
  Register #(.width(64)) rcx_1 (.D(multiplexer_2_out), .en(decmux_2_enable), .clk(clk), .Q(rcx_1_q));  // open: clr
  Register #(.width(64)) rdx_2 (.D(multiplexer_3_out), .en(decmux_3_enable), .clk(clk), .Q(rdx_2_q));  // open: clr
  Register #(.width(64)) rbx_3 (.D(multiplexer_4_out), .en(decmux_4_enable), .clk(clk), .Q(rbx_3_q));  // open: clr
  Register #(.width(64)) rsp_4 (.D(multiplexer_5_out), .en(decmux_5_enable), .clk(clk), .Q(rsp_4_q));  // open: clr
  Register #(.width(64)) rbp_5 (.D(multiplexer_6_out), .en(decmux_6_enable), .clk(clk), .Q(rbp_5_q));  // open: clr
  Register #(.width(64)) rsi_6 (.D(multiplexer_7_out), .en(decmux_7_enable), .clk(clk), .Q(rsi_6_q));  // open: clr
  Register #(.width(64)) rdi_7 (.D(multiplexer_8_out), .en(decmux_8_enable), .clk(clk), .Q(rdi_7_q));  // open: clr
  Register #(.width(64)) r8_8 (.D(multiplexer_9_out), .en(decmux_9_enable), .clk(clk), .Q(r8_8_q));  // open: clr
  Register #(.width(64)) r9 (.D(multiplexer_10_out), .en(decmux_10_enable), .clk(clk), .Q(r9_q));  // open: clr
  Register #(.width(64)) r10 (.D(multiplexer_11_out), .en(decmux_11_enable), .clk(clk), .Q(r10_q));  // open: clr
  Register #(.width(64)) r11 (.D(multiplexer_12_out), .en(decmux_12_enable), .clk(clk), .Q(r11_q));  // open: clr
  Register #(.width(64)) r12 (.D(multiplexer_13_out), .en(decmux_13_enable), .clk(clk), .Q(r12_q));  // open: clr
  Register #(.width(64)) r13 (.D(multiplexer_14_out), .en(decmux_14_enable), .clk(clk), .Q(r13_q));  // open: clr
  Register #(.width(64)) r14 (.D(multiplexer_15_out), .en(decmux_15_enable), .clk(clk), .Q(r14_q));  // open: clr
  assign ValA = srcA_decode_r0 ? rax_0_q : 64'bz;  // Controlled_Buffer controlled_buffer_1
  assign ValA = srcA_decode_r1 ? rcx_1_q : 64'bz;  // Controlled_Buffer controlled_buffer_2
  assign ValA = srcA_decode_r2 ? rdx_2_q : 64'bz;  // Controlled_Buffer controlled_buffer_3
  assign ValA = srcA_decode_r3 ? rbx_3_q : 64'bz;  // Controlled_Buffer controlled_buffer_4
  assign ValB = srcB_decode_r0 ? rax_0_q : 64'bz;  // Controlled_Buffer controlled_buffer_5
  assign ValB = srcB_decode_r1 ? rcx_1_q : 64'bz;  // Controlled_Buffer controlled_buffer_6
  assign ValB = srcB_decode_r2 ? rdx_2_q : 64'bz;  // Controlled_Buffer controlled_buffer_7
  assign ValB = srcB_decode_r3 ? rbx_3_q : 64'bz;  // Controlled_Buffer controlled_buffer_8
  assign ValB = srcB_decode_r4 ? rsp_4_q : 64'bz;  // Controlled_Buffer controlled_buffer_9
  assign ValB = srcB_decode_r5 ? rbp_5_q : 64'bz;  // Controlled_Buffer controlled_buffer_10
  assign ValB = srcB_decode_r6 ? rsi_6_q : 64'bz;  // Controlled_Buffer controlled_buffer_11
  Controlled_Buffer #(.width(64)) controlled_buffer_12 (.in(rdi_7_q), .en(srcB_decode_r7));  // open: out
  assign ValB = srcB_decode_r8 ? r8_8_q : 64'bz;  // Controlled_Buffer controlled_buffer_13
  assign ValB = srcB_decode_r9 ? r9_q : 64'bz;  // Controlled_Buffer controlled_buffer_14
  assign ValB = srcB_decode_r10 ? r10_q : 64'bz;  // Controlled_Buffer controlled_buffer_15
  assign ValB = srcB_decode_r11 ? r11_q : 64'bz;  // Controlled_Buffer controlled_buffer_16
  assign ValB = srcB_decode_r12 ? r12_q : 64'bz;  // Controlled_Buffer controlled_buffer_17
  assign ValB = srcB_decode_r13 ? r13_q : 64'bz;  // Controlled_Buffer controlled_buffer_18
  assign ValB = srcB_decode_r14 ? r14_q : 64'bz;  // Controlled_Buffer controlled_buffer_19
  assign ValA = srcA_decode_r4 ? rsp_4_q : 64'bz;  // Controlled_Buffer controlled_buffer_20
  assign ValA = srcA_decode_r5 ? rbp_5_q : 64'bz;  // Controlled_Buffer controlled_buffer_21
  assign ValA = srcA_decode_r6 ? rsi_6_q : 64'bz;  // Controlled_Buffer controlled_buffer_22
  assign ValA = srcA_decode_r7 ? rdi_7_q : 64'bz;  // Controlled_Buffer controlled_buffer_23
  assign ValA = srcA_decode_r8 ? r8_8_q : 64'bz;  // Controlled_Buffer controlled_buffer_24
  assign ValA = srcA_decode_r9 ? r9_q : 64'bz;  // Controlled_Buffer controlled_buffer_25
  assign ValA = srcA_decode_r10 ? r10_q : 64'bz;  // Controlled_Buffer controlled_buffer_26
  assign ValA = srcA_decode_r11 ? r11_q : 64'bz;  // Controlled_Buffer controlled_buffer_27
  assign ValA = srcA_decode_r12 ? r12_q : 64'bz;  // Controlled_Buffer controlled_buffer_28
  assign ValA = srcA_decode_r13 ? r13_q : 64'bz;  // Controlled_Buffer controlled_buffer_29
  assign ValA = srcA_decode_r14 ? r14_q : 64'bz;  // Controlled_Buffer controlled_buffer_30
  addr_decode srcB_decode (
    .src(icodetoinputvals_1_srcb), .r0(srcB_decode_r0), .r1(srcB_decode_r1), .r2(srcB_decode_r2),
    .r3(srcB_decode_r3), .r4(srcB_decode_r4), .r5(srcB_decode_r5), .r6(srcB_decode_r6), .r7(srcB_decode_r7),
    .r8(srcB_decode_r8), .r9(srcB_decode_r9), .r10(srcB_decode_r10), .r11(srcB_decode_r11),
    .r12(srcB_decode_r12), .r13(srcB_decode_r13), .r14(srcB_decode_r14));
  addr_decode srcA_decode (
    .src(icodetoinputvals_1_srca), .r0(srcA_decode_r0), .r1(srcA_decode_r1), .r2(srcA_decode_r2),
    .r3(srcA_decode_r3), .r4(srcA_decode_r4), .r5(srcA_decode_r5), .r6(srcA_decode_r6), .r7(srcA_decode_r7),
    .r8(srcA_decode_r8), .r9(srcA_decode_r9), .r10(srcA_decode_r10), .r11(srcA_decode_r11),
    .r12(srcA_decode_r12), .r13(srcA_decode_r13), .r14(srcA_decode_r14));
endmodule

module Execute (
  input  [63:0] valC,
  input  [63:0] valA,
  input  [3:0] icode,
  input  [63:0] valB,
  input  [3:0] ifun,
  input  clk,
  output [63:0] valE,
  output cnd
);

  wire alu_1_cf, alu_1_o_f, alu_1_sf, alu_1_zf, alubselector_1_s0, multiplexer_4_out, OO_q, opq_out,
       or_1_out, SS_q, ZZ_q;
  wire [1:0] aluaselector_1_s1;
  wire [3:0] multiplexer_1_out;
  wire [63:0] multiplexer_2_out, multiplexer_3_out;

  Multiplexer #(.width(4)) multiplexer_1 (.in0(4'b0000), .in1(ifun), .out(multiplexer_1_out), .sel(opq_out));
  and opq (opq_out, ~icode[0], icode[1], icode[2], ~icode[3]);  // AND_Gate
  ALUASelector aluaselector_1 (.icode(icode), .s1(aluaselector_1_s1[0]), .s0(aluaselector_1_s1[1]));
  Multiplexer #(.width(64)) multiplexer_2 (
    .in0({64{1'b0}}), .in1(valB), .out(multiplexer_2_out), .sel(alubselector_1_s0));
  ALUBSelector alubselector_1 (.icode(icode), .s0(alubselector_1_s0));
  Multiplexer #(.select(2), .width(64)) multiplexer_3 (
    .in0(valA), .in1(valC), .in2(64'h8), .in3(64'hfffffffffffffff8), .out(multiplexer_3_out),
    .sel(aluaselector_1_s1));
  Multiplexer multiplexer_4 (.in0(OO_q), .in1(or_1_out), .out(multiplexer_4_out), .sel(opq_out));
  Multiplexer multiplexer_5 (.in0(SS_q), .in1(alu_1_sf), .out(clk), .sel(opq_out));
  Multiplexer multiplexer_6 (.in0(ZZ_q), .in1(alu_1_zf), .out(clk), .sel(opq_out));
  or or_1 (or_1_out, alu_1_o_f, alu_1_cf);
  D_Flip_Flop OO (.D(multiplexer_4_out), .clk(clk), .Q(OO_q));  // open: Qn, preset, reset
  D_Flip_Flop SS (.D(clk), .clk(clk), .Q(SS_q));  // open: Qn, preset, reset
  D_Flip_Flop ZZ (.D(clk), .clk(clk), .Q(ZZ_q));  // open: Qn, preset, reset
  ALU alu_1 (
    .A(multiplexer_3_out), .B(multiplexer_2_out), .fun(multiplexer_1_out), .CF(alu_1_cf), .O_F(alu_1_o_f),
    .SF(alu_1_sf), .valE(valE), .ZF(alu_1_zf));
  cond cond_1 (.O_F(OO_q), .SF(SS_q), .ZF(ZZ_q), .ifun(ifun), .condi(cnd));
endmodule

module Memory (
  input  [3:0] icode,
  input  [63:0] valE,
  input  [63:0] valA,
  input  [63:0] valP,
  input  clk,
  output dmem_error,
  output [63:0] valM
);

  wire memaddress_1_out_3, memdata_1_out_3, memread_1_read, memwrite_1_write, not_1_out, not_2_out;
  wire [63:0] controlled_buffer_1_out, controlled_buffer_2_out;

  assign controlled_buffer_1_out = memaddress_1_out_3 ? valA : 64'bz;  // Controlled_Buffer controlled_buffer_1
  assign controlled_buffer_2_out = memdata_1_out_3 ? valP : 64'bz;  // Controlled_Buffer controlled_buffer_2
  MemAddress memaddress_1 (.icode(icode), .clk(clk), .out_3(memaddress_1_out_3));
  MemData memdata_1 (.icode(icode), .clk(clk), .out_3(memdata_1_out_3));
  MemRead memread_1 (.icode(icode), .clk(clk), .read(memread_1_read));
  MemWrite memwrite_1 (.icode(icode), .clk(clk), .write(memwrite_1_write));
  assign controlled_buffer_1_out = not_1_out ? valE : 64'bz;  // Controlled_Buffer controlled_buffer_3
  not not_1 (not_1_out, memaddress_1_out_3);
  assign controlled_buffer_2_out = not_2_out ? valA : 64'bz;  // Controlled_Buffer controlled_buffer_4
  not not_2 (not_2_out, memdata_1_out_3);
  DataMemory datamemory_1 (
    .wen(memwrite_1_write), .ren(memread_1_read), .addr(controlled_buffer_1_out[11:0]),
    .data(controlled_buffer_2_out), .clk(clk), .dmem_error(dmem_error), .valM(valM));

  // Notes on the sheet:
  //   14
  //   15, 16-23
endmodule

module PCUpdate (
  input  [3:0] icode,
  input  cnd,
  input  [63:0] valC,
  input  [63:0] valM,
  input  [63:0] valP,
  input  clk,
  output [63:0] PC
);

  wire and_1_out, and_2_out, and_3_out, and_4_out, and_5_out, comparator_1_eq, not_1_out, not_2_out, or_1_out;
  wire [4:0] counter_1_q;
  wire [63:0] controlled_buffer_1_out;

  and and_1 (and_1_out, icode[0], icode[1], icode[2], ~icode[3]);  // AND_Gate
  and and_2 (and_2_out, and_1_out, cnd);
  and and_3 (and_3_out, ~icode[0], ~icode[1], ~icode[2], icode[3]);  // AND_Gate
  or or_1 (or_1_out, and_2_out, and_3_out);
  assign controlled_buffer_1_out = or_1_out ? valC : 64'bz;  // Controlled_Buffer controlled_buffer_1
  not not_1 (not_1_out, or_1_out);
  and and_4 (and_4_out, icode[0], ~icode[1], ~icode[2], icode[3]);  // AND_Gate
  not not_2 (not_2_out, and_4_out);
  assign controlled_buffer_1_out = and_4_out ? valM : 64'bz;  // Controlled_Buffer controlled_buffer_2
  and and_5 (and_5_out, not_1_out, not_2_out);
  assign controlled_buffer_1_out = and_5_out ? valP : 64'bz;  // Controlled_Buffer controlled_buffer_3
  Register #(.width(64)) register_1 (
    .D(controlled_buffer_1_out), .en(comparator_1_eq), .clk(clk), .Q(PC));  // open: clr
  Comparator #(.width(5)) comparator_1 (.a(5'b11001), .b(counter_1_q), .eq(comparator_1_eq));  // open: gt, lt
  Counter_part #(.max('h1a), .width(5)) counter_1 (.clk(clk), .Q(counter_1_q));  // open: clr, load, up, count, D, carry
endmodule

module InstructionMemory (
  input  [63:0] PC,
  input  clk,
  output [7:0] b1,
  output [7:0] b2,
  output [7:0] b3,
  output [7:0] b4,
  output [7:0] b5,
  output [7:0] b6,
  output [7:0] b7,
  output [7:0] b8,
  output [7:0] b9,
  output [7:0] b0,
  output imem_error
);

  wire comparator_1_lt, comparator_2_eq, counter_3_b0, counter_3_b1, counter_3_b2, counter_3_b3,
       counter_3_b4, counter_3_b5, counter_3_b6, counter_3_b7, counter_3_b8, counter_3_b9;
  wire [7:0] controlled_buffer_1_out, controlled_buffer_2_out, controlled_buffer_3_out,
       controlled_buffer_4_out, controlled_buffer_5_out, controlled_buffer_6_out, controlled_buffer_7_out,
       controlled_buffer_8_out, controlled_buffer_9_out, controlled_buffer_10_out, register_1_q,
       register_2_q, register_3_q, register_4_q, register_5_q, register_6_q, register_7_q, register_8_q,
       register_9_q, register_10_q, rom_1_data;
  wire [11:0] adder_1_out, counter_1_q, counter_2_q;

  Counter_part #(.max('h1a), .width(12)) counter_1 (
    .clk(clk), .Q(counter_1_q));  // open: clr, load, up, count, D, carry
  ROM #(.addrWidth(12)) rom_1 (.addr(adder_1_out), .data(rom_1_data));
  Comparator #(.width(12)) comparator_1 (.a(counter_1_q), .b(12'ha), .lt(comparator_1_lt));  // open: gt, eq
  Counter_part #(.max('h9), .width(12)) counter_2 (
    .count(comparator_1_lt), .clk(clk), .Q(counter_2_q));  // open: clr, load, up, D, carry
  Counter counter_3 (
    .i0(counter_2_q[3]), .i1(counter_2_q[2]), .i2(counter_2_q[1]), .i3(counter_2_q[0]), .b0(counter_3_b0),
    .b1(counter_3_b1), .b2(counter_3_b2), .b3(counter_3_b3), .b4(counter_3_b4), .b5(counter_3_b5),
    .b6(counter_3_b6), .b7(counter_3_b7), .b8(counter_3_b8), .b9(counter_3_b9));
  assign controlled_buffer_1_out = counter_3_b9 ? rom_1_data : 8'bz;  // Controlled_Buffer controlled_buffer_1
  assign controlled_buffer_2_out = counter_3_b8 ? rom_1_data : 8'bz;  // Controlled_Buffer controlled_buffer_2
  assign controlled_buffer_3_out = counter_3_b7 ? rom_1_data : 8'bz;  // Controlled_Buffer controlled_buffer_3
  assign controlled_buffer_4_out = counter_3_b6 ? rom_1_data : 8'bz;  // Controlled_Buffer controlled_buffer_4
  assign controlled_buffer_5_out = counter_3_b5 ? rom_1_data : 8'bz;  // Controlled_Buffer controlled_buffer_5
  assign controlled_buffer_6_out = counter_3_b4 ? rom_1_data : 8'bz;  // Controlled_Buffer controlled_buffer_6
  assign controlled_buffer_7_out = counter_3_b3 ? rom_1_data : 8'bz;  // Controlled_Buffer controlled_buffer_7
  assign controlled_buffer_8_out = counter_3_b2 ? rom_1_data : 8'bz;  // Controlled_Buffer controlled_buffer_8
  Adder #(.width(12)) adder_1 (.a(PC[11:0]), .b(counter_2_q), .out(adder_1_out), .cout(imem_error));  // open: cin
  assign controlled_buffer_9_out = counter_3_b1 ? rom_1_data : 8'bz;  // Controlled_Buffer controlled_buffer_9
  assign controlled_buffer_10_out = counter_3_b0 ? rom_1_data : 8'bz;  // Controlled_Buffer controlled_buffer_10
  Register register_1 (.D(controlled_buffer_9_out), .en(counter_3_b1), .clk(clk), .Q(register_1_q));  // open: clr
  Register register_2 (.D(controlled_buffer_8_out), .en(counter_3_b2), .clk(clk), .Q(register_2_q));  // open: clr
  Register register_3 (.D(controlled_buffer_7_out), .en(counter_3_b3), .clk(clk), .Q(register_3_q));  // open: clr
  Register register_4 (.D(controlled_buffer_6_out), .en(counter_3_b4), .clk(clk), .Q(register_4_q));  // open: clr
  Register register_5 (.D(controlled_buffer_5_out), .en(counter_3_b5), .clk(clk), .Q(register_5_q));  // open: clr
  Register register_6 (.D(controlled_buffer_4_out), .en(counter_3_b6), .clk(clk), .Q(register_6_q));  // open: clr
  Register register_7 (.D(controlled_buffer_3_out), .en(counter_3_b7), .clk(clk), .Q(register_7_q));  // open: clr
  Register register_8 (.D(controlled_buffer_2_out), .en(counter_3_b8), .clk(clk), .Q(register_8_q));  // open: clr
  Register register_9 (.D(controlled_buffer_1_out), .en(counter_3_b9), .clk(clk), .Q(register_9_q));  // open: clr
  Register register_10 (.D(controlled_buffer_10_out), .en(counter_3_b0), .clk(clk), .Q(register_10_q));  // open: clr
  Comparator #(.width(12)) comparator_2 (.a(counter_2_q), .b(12'h9), .eq(comparator_2_eq));  // open: gt, lt
  assign b9 = comparator_2_eq ? register_9_q : 8'bz;  // Controlled_Buffer controlled_buffer_11
  assign b0 = comparator_2_eq ? register_10_q : 8'bz;  // Controlled_Buffer controlled_buffer_12
  assign b6 = comparator_2_eq ? register_6_q : 8'bz;  // Controlled_Buffer controlled_buffer_13
  assign b7 = comparator_2_eq ? register_7_q : 8'bz;  // Controlled_Buffer controlled_buffer_14
  assign b8 = comparator_2_eq ? register_8_q : 8'bz;  // Controlled_Buffer controlled_buffer_15
  assign b4 = comparator_2_eq ? register_4_q : 8'bz;  // Controlled_Buffer controlled_buffer_16
  assign b5 = comparator_2_eq ? register_5_q : 8'bz;  // Controlled_Buffer controlled_buffer_17
  assign b2 = comparator_2_eq ? register_2_q : 8'bz;  // Controlled_Buffer controlled_buffer_18
  assign b3 = comparator_2_eq ? register_3_q : 8'bz;  // Controlled_Buffer controlled_buffer_19
  assign b1 = comparator_2_eq ? register_1_q : 8'bz;  // Controlled_Buffer controlled_buffer_20

  // Notes on the sheet:
  //   contents of rom_1 (hex, n*v repeats v):
  //   30 f4 e8 3 6*0 80 1e 7*0 30 f0 1 8*0 30 f8 1 7*0 30 f9 2 7*0 30 fa 3 7*0 30 fb 4 7*0 30 fc 5 7*0 30
  //   fd 6 7*0 30 fe 7 7*0 30 f6 8 7*0 30 f8 1 7*0 30 f9 2 7*0 30 fa 3 7*0 30 fb 4 7*0 30 fc 5 7*0 30 fd 6
  //   7*0 30 fe 7 7*0 30 f6 8 7*0 20 c5 60 e5 60 e5 20 d3 60 63 60 63 20 c2 60 c2 60 c2 60 e2 60 e2 60 e2
  //   60 e2 20 d1 60 d1 60 d1 60 61 60 61 60 61 60 61 90
endmodule

module Counter (
  input  i0,
  input  i1,
  input  i2,
  input  i3,
  output b0,
  output b1,
  output b2,
  output b3,
  output b4,
  output b5,
  output b6,
  output b7,
  output b8,
  output b9
);

  wire not_1_out, not_2_out, not_3_out, not_4_out;

  not not_1 (not_1_out, i0);
  not not_2 (not_2_out, i1);
  not not_3 (not_3_out, i2);
  not not_4 (not_4_out, i3);
  and and_1 (b0, not_1_out, not_2_out, not_3_out, not_4_out);
  and and_2 (b1, not_1_out, not_2_out, not_3_out, i3);
  and and_3 (b2, not_1_out, not_2_out, i2, not_4_out);
  and and_4 (b3, not_1_out, not_2_out, i2, i3);
  and and_5 (b4, not_1_out, i1, not_3_out, not_4_out);
  and and_6 (b5, not_1_out, i1, not_3_out, i3);
  and and_7 (b6, not_1_out, i1, i2, not_4_out);
  and and_8 (b7, not_1_out, i1, i2, i3);
  and and_9 (b8, i0, not_2_out, not_3_out, not_4_out);
  and and_10 (b9, i0, not_2_out, not_3_out, i3);
endmodule

module Align (
  input  [3:0] code,
  output ifun,
  output NeedRegids,
  output NeedValC
);

  wire and_1_out, and_2_out, and_3_out, and_4_out, and_5_out, and_6_out, and_7_out, and_8_out, not_1_out,
       not_2_out, not_3_out, not_4_out;

  not not_1 (not_1_out, code[3]);
  not not_2 (not_2_out, code[2]);
  not not_3 (not_3_out, code[1]);
  not not_4 (not_4_out, code[0]);
  and and_1 (and_1_out, not_1_out, code[1], not_4_out);
  and and_2 (and_2_out, not_1_out, code[2], code[1]);
  and and_3 (and_3_out, not_2_out, code[1]);
  and and_4 (and_4_out, not_1_out, code[2], not_3_out);
  and and_5 (and_5_out, not_1_out, code[2], not_4_out);
  and and_6 (and_6_out, not_1_out, code[2], not_3_out);
  and and_7 (and_7_out, code[3], not_2_out, not_3_out, not_4_out);
  and and_8 (and_8_out, not_1_out, code[1], code[0]);
  or or_1 (ifun, and_1_out, and_2_out);
  or or_2 (NeedRegids, and_3_out, and_4_out, and_5_out);
  or or_3 (NeedValC, and_6_out, and_7_out, and_8_out);
endmodule

module Split (
  input  [7:0] in_1,
  output [3:0] icode,
  output [3:0] ifun,
  output invalid_instr
);

  MemError memerror_1 (.code(in_1[3:0]), .invalid_instr(invalid_instr));

  assign icode = in_1[7:4];
  assign ifun = in_1[3:0];
endmodule

module MemError (
  input  [3:0] code,
  output invalid_instr
);

  and and_1 (invalid_instr, code[3], code[2]);
endmodule

module PCIncrement (
  input  [63:0] PC,
  input  needs_reg,
  input  needs_valC,
  output [63:0] PC0
);

  wire [3:0] adder_1_out, adder_2_out, multiplier_1_out;

  Adder #(.width(4)) adder_1 (.a({3'b000, needs_reg}), .b(4'b0001), .out(adder_1_out));  // open: cin, cout
  Multiplier #(.width(4)) multiplier_1 (
    .a({3'b000, needs_valC}), .b(4'b1000), .out(multiplier_1_out));  // open: cin, cout
  Adder #(.width(4)) adder_2 (.a(adder_1_out), .b(multiplier_1_out), .out(adder_2_out));  // open: cin, cout
  Adder #(.width(64)) adder_3 (.a(PC), .b({{60{1'b0}}, adder_2_out}), .out(PC0));  // open: cin, cout
endmodule

module ALUASelector (
  input  [3:0] icode,
  output s1,
  output s0
);

  wire and_2_out, and_3_out, and_4_out, not_1_out, not_2_out, not_3_out, not_4_out;

  not not_1 (not_1_out, icode[3]);
  not not_2 (not_2_out, icode[2]);
  not not_3 (not_3_out, icode[1]);
  not not_4 (not_4_out, icode[0]);
  and and_1 (s0, icode[3], not_2_out);
  and and_2 (and_2_out, not_1_out, not_2_out, icode[1], icode[0]);
  and and_3 (and_3_out, not_1_out, icode[2], not_3_out);
  and and_4 (and_4_out, icode[3], not_2_out, not_4_out);
  or or_1 (s1, and_2_out, and_3_out, and_4_out);
endmodule

module ALUBSelector (
  input  [3:0] icode,
  output s0
);

  wire and_1_out, and_2_out, and_3_out, not_1_out, not_2_out, not_3_out, not_4_out;

  not not_1 (not_1_out, icode[3]);
  not not_2 (not_2_out, icode[2]);
  not not_3 (not_3_out, icode[1]);
  not not_4 (not_4_out, icode[0]);
  and and_1 (and_1_out, not_1_out, icode[2], not_3_out);
  and and_2 (and_2_out, not_1_out, icode[2], not_4_out);
  and and_3 (and_3_out, icode[3], not_2_out);
  or or_1 (s0, and_1_out, and_2_out, and_3_out);
endmodule

module ALU (
  input  [63:0] A,
  input  [63:0] B,
  input  [3:0] fun,
  output CF,
  output O_F,
  output SF,
  output [63:0] valE,
  output ZF
);

  wire [63:0] adder_1_out, and_1_out, subtractor_1_out, xor_1_out;

  Adder #(.width(64)) adder_1 (.a(A), .b(B), .out(adder_1_out));  // open: cin, cout
  Subtractor #(.width(64)) subtractor_1 (.a(B), .b(A), .out(subtractor_1_out));  // open: bin, bout
  assign and_1_out = A & B;  // AND_Gate and_1, 64 bits wide
  assign xor_1_out = A ^ B;  // XOR_Gate xor_1, 64 bits wide
  overflowAdd overflowadd_1 (.valA(A), .valB(B), .reuslt(adder_1_out), .posOverflow(CF), .negOverflow(O_F));
  Multiplexer #(.select(2), .width(64)) multiplexer_1 (
    .in0(adder_1_out), .in1(subtractor_1_out), .in2(and_1_out), .in3(xor_1_out), .out(valE), .sel(fun[1:0]));
  Comparator #(.width(64)) comparator_1 (.a(valE), .b({64{1'b0}}), .lt(SF));  // open: gt, eq
  Comparator #(.width(64)) comparator_2 (.a(valE), .b({64{1'b0}}), .eq(ZF));  // open: gt, lt
endmodule

module overflowAdd (
  input  [63:0] valA,
  input  [63:0] valB,
  input  [63:0] reuslt,
  output posOverflow,
  output negOverflow
);

  wire and_1_out, and_2_out, and_4_out, not_1_out, xor_1_out;

  not not_1 (not_1_out, valB[63]);
  and and_1 (and_1_out, valA[63], valB[63]);
  and and_2 (and_2_out, not_1_out, reuslt[63]);
  and and_3 (posOverflow, and_1_out, and_2_out);
  and and_4 (and_4_out, reuslt[63], valA[63]);
  xor xor_1 (xor_1_out, valB[63], valA[63]);
  and and_5 (negOverflow, and_4_out, xor_1_out);
endmodule

module zero (
  input  [7:0] result,
  input  [1:0] ifun,
  input  [63:0] reuslt,
  output s0
);

  wire and_1_out, and_2_out, not_1_out, not_2_out, not_3_out, not_4_out, not_5_out, not_6_out, not_7_out,
       not_8_out;

  not not_1 (not_1_out, result[7]);
  not not_2 (not_2_out, result[6]);
  not not_3 (not_3_out, result[5]);
  not not_4 (not_4_out, result[3]);
  not not_5 (not_5_out, result[2]);
  not not_6 (not_6_out, result[1]);
  not not_7 (not_7_out, result[0]);
  not not_8 (not_8_out, ifun[1]);
  and and_1 (and_1_out, not_1_out, not_2_out, not_3_out, not_4_out, not_5_out, not_6_out, not_7_out, not_8_out, ifun[0]);
  and and_2 (and_2_out, not_1_out, not_2_out, not_3_out, not_4_out, result[2], result[1], not_7_out);
  or or_1 (s0, and_1_out, and_2_out);

  // Notes on the sheet:
  //   1 0
endmodule

module cond (
  input  O_F,
  input  SF,
  input  ZF,
  input  [3:0] ifun,
  output condi
);

  wire jump_1_je, jump_1_jg, jump_1_jge, jump_1_jl, jump_1_jle, jump_1_jmp, jump_1_jne;

  // XOR_Gate xor_1 is placed but not wired
  jump jump_1 (
    .o(O_F), .s(SF), .z(ZF), .jmp(jump_1_jmp), .jle(jump_1_jle), .jl(jump_1_jl), .je(jump_1_je),
    .jne(jump_1_jne), .jge(jump_1_jge), .jg(jump_1_jg));
  Multiplexer #(.select(3)) multiplexer_1 (
    .in0(jump_1_jmp), .in1(jump_1_jle), .in2(jump_1_jl), .in3(jump_1_je), .in4(jump_1_jne), .in5(jump_1_jge),
    .in6(jump_1_jg), .out(condi), .sel(ifun[2:0]));  // open: in7
endmodule

module jump (
  input  o,
  input  s,
  input  z,
  output jmp,
  output jle,
  output jl,
  output je,
  output jne,
  output jge,
  output jg
);

  wire and_4_out, and_5_out, and_6_out, and_7_out, and_8_out, and_9_out, and_10_out, and_11_out, not_1_out,
       not_2_out, not_3_out, or_1_out, or_2_out, or_3_out, or_4_out;

  not not_1 (not_1_out, o);
  not not_2 (not_2_out, s);
  not not_3 (not_3_out, z);
  and and_1 (jmp, 1'b1, 1'b1);
  and and_2 (je, z, 1'b1);
  and and_3 (jne, not_3_out, 1'b1);
  and and_4 (and_4_out, s, o);
  and and_5 (and_5_out, not_2_out, not_1_out);
  and and_6 (and_6_out, s, o);
  and and_7 (and_7_out, not_2_out, not_1_out);
  and and_8 (and_8_out, s, not_1_out);
  and and_9 (and_9_out, not_2_out, o);
  and and_10 (and_10_out, s, not_1_out);
  and and_11 (and_11_out, not_2_out, o);
  or or_1 (or_1_out, and_4_out, and_5_out);
  or or_2 (or_2_out, and_6_out, and_7_out);
  or or_3 (or_3_out, and_8_out, and_9_out);
  or or_4 (or_4_out, and_10_out, and_11_out, z);
  and and_12 (jg, or_1_out, not_3_out, 1'b1);
  and and_13 (jge, or_2_out, 1'b1);
  and and_14 (jl, or_3_out, 1'b1);
  and and_15 (jle, or_4_out, 1'b1);
endmodule

module DataMemory (
  input  wen,
  input  ren,
  input  [11:0] addr,
  input  [63:0] data,
  input  clk,
  output dmem_error,
  output [63:0] valM
);

  wire and_1_out, and_2_out, comparator_1_eq, comparator_2_lt, comparator_3_gt, comparator_4_gt,
       comparator_5_lt, comparator_6_eq, controlled_buffer_1_out, memcounter_1_b1, memcounter_1_b2,
       memcounter_1_b3, memcounter_1_b4, memcounter_1_b5, memcounter_1_b6, memcounter_1_b7, memcounter_1_b8;
  wire [2:0] counter_1_q;
  wire [7:0] controlled_buffer_2_out, controlled_buffer_3_out, controlled_buffer_4_out,
       controlled_buffer_5_out, controlled_buffer_6_out, controlled_buffer_7_out, controlled_buffer_8_out,
       controlled_buffer_9_out, multiplexer_1_out, ram_1_dout, register_1_q, register_2_q, register_3_q,
       register_4_q, register_5_q, register_6_q, register_7_q, register_8_q;
  wire [8:0] counter_1_q_2;
  wire [11:0] adder_1_out, counter_2_q, undriven;

  Comparator #(.width(12)) comparator_1 (.a(counter_2_q), .b(12'hf), .eq(comparator_1_eq));  // open: gt, lt
  Counter_part #(.max('h8), .width(12)) counter_1 (
    .clr(comparator_1_eq), .count(and_2_out), .clk(clk), .D(undriven), .Q({counter_1_q_2, counter_1_q}));  // open: load, up, carry
  assign controlled_buffer_1_out = and_1_out ? wen : 1'bz;  // Controlled_Buffer controlled_buffer_1
  Adder #(.width(12)) adder_1 (
    .a(addr), .b({counter_1_q_2, counter_1_q}), .out(adder_1_out), .cout(dmem_error));  // open: cin
  Multiplexer #(.select(3), .width(8)) multiplexer_1 (
    .in0(data[7:0]), .in1(data[15:8]), .in2(data[23:16]), .in3(data[31:24]), .in4(data[39:32]),
    .in5(data[47:40]), .in6(data[55:48]), .in7(data[63:56]), .out(multiplexer_1_out), .sel(counter_1_q));
  RAM #(.addrWidth(12)) ram_1 (
    .addr(adder_1_out), .we(controlled_buffer_1_out), .oe(ren), .clk(clk), .din(multiplexer_1_out),
    .dout(ram_1_dout));
  Counter_part #(.max('h1a), .width(12)) counter_2 (
    .clk(clk), .Q(counter_2_q));  // open: clr, load, up, count, D, carry
  MemCounter memcounter_1 (
    .i0(counter_1_q_2[0]), .i1(counter_1_q[2]), .i2(counter_1_q[1]), .i3(counter_1_q[0]),
    .b1(memcounter_1_b1), .b2(memcounter_1_b2), .b3(memcounter_1_b3), .b4(memcounter_1_b4),
    .b5(memcounter_1_b5), .b6(memcounter_1_b6), .b7(memcounter_1_b7), .b8(memcounter_1_b8));  // open: b0
  assign controlled_buffer_2_out = memcounter_1_b8 ? ram_1_dout : 8'bz;  // Controlled_Buffer controlled_buffer_2
  assign controlled_buffer_3_out = memcounter_1_b7 ? ram_1_dout : 8'bz;  // Controlled_Buffer controlled_buffer_3
  assign controlled_buffer_4_out = memcounter_1_b6 ? ram_1_dout : 8'bz;  // Controlled_Buffer controlled_buffer_4
  assign controlled_buffer_5_out = memcounter_1_b5 ? ram_1_dout : 8'bz;  // Controlled_Buffer controlled_buffer_5
  assign controlled_buffer_6_out = memcounter_1_b4 ? ram_1_dout : 8'bz;  // Controlled_Buffer controlled_buffer_6
  assign controlled_buffer_7_out = memcounter_1_b3 ? ram_1_dout : 8'bz;  // Controlled_Buffer controlled_buffer_7
  assign controlled_buffer_8_out = memcounter_1_b2 ? ram_1_dout : 8'bz;  // Controlled_Buffer controlled_buffer_8
  Comparator #(.width(12)) comparator_2 (.a(counter_2_q), .b(12'h18), .lt(comparator_2_lt));  // open: gt, eq
  Comparator #(.width(12)) comparator_3 (.a(counter_2_q), .b(12'he), .gt(comparator_3_gt));  // open: eq, lt
  Comparator #(.width(12)) comparator_4 (.a(counter_2_q), .b(12'hf), .gt(comparator_4_gt));  // open: eq, lt
  Comparator #(.width(12)) comparator_5 (.a(counter_2_q), .b(12'h18), .lt(comparator_5_lt));  // open: gt, eq
  assign controlled_buffer_9_out = memcounter_1_b1 ? ram_1_dout : 8'bz;  // Controlled_Buffer controlled_buffer_9
  and and_1 (and_1_out, comparator_2_lt, comparator_3_gt);
  and and_2 (and_2_out, comparator_4_gt, comparator_5_lt);
  Register register_1 (.D(controlled_buffer_9_out), .en(memcounter_1_b1), .clk(clk), .Q(register_1_q));  // open: clr
  Register register_2 (.D(controlled_buffer_8_out), .en(memcounter_1_b2), .clk(clk), .Q(register_2_q));  // open: clr
  Register register_3 (.D(controlled_buffer_7_out), .en(memcounter_1_b3), .clk(clk), .Q(register_3_q));  // open: clr
  Register register_4 (.D(controlled_buffer_6_out), .en(memcounter_1_b4), .clk(clk), .Q(register_4_q));  // open: clr
  Register register_5 (.D(controlled_buffer_5_out), .en(memcounter_1_b5), .clk(clk), .Q(register_5_q));  // open: clr
  Register register_6 (.D(controlled_buffer_4_out), .en(memcounter_1_b6), .clk(clk), .Q(register_6_q));  // open: clr
  Register register_7 (.D(controlled_buffer_3_out), .en(memcounter_1_b7), .clk(clk), .Q(register_7_q));  // open: clr
  Register register_8 (.D(controlled_buffer_2_out), .en(memcounter_1_b8), .clk(clk), .Q(register_8_q));  // open: clr
  Comparator #(.width(12)) comparator_6 (.a(counter_2_q), .b(12'h19), .eq(comparator_6_eq));  // open: gt, lt
  assign valM[55:48] = comparator_6_eq ? register_7_q : 8'bz;  // Controlled_Buffer controlled_buffer_10
  assign valM[63:56] = comparator_6_eq ? register_8_q : 8'bz;  // Controlled_Buffer controlled_buffer_11
  assign valM[39:32] = comparator_6_eq ? register_5_q : 8'bz;  // Controlled_Buffer controlled_buffer_12
  assign valM[47:40] = comparator_6_eq ? register_6_q : 8'bz;  // Controlled_Buffer controlled_buffer_13
  assign valM[15:8] = comparator_6_eq ? register_2_q : 8'bz;  // Controlled_Buffer controlled_buffer_14
  assign valM[23:16] = comparator_6_eq ? register_3_q : 8'bz;  // Controlled_Buffer controlled_buffer_15
  assign valM[31:24] = comparator_6_eq ? register_4_q : 8'bz;  // Controlled_Buffer controlled_buffer_16
  assign valM[7:0] = comparator_6_eq ? register_1_q : 8'bz;  // Controlled_Buffer controlled_buffer_17
endmodule

module MemRead (
  input  [3:0] icode,
  input  clk,
  output read
);

  wire and_1_out, and_2_out, comparator_1_eq, not_1_out, not_2_out, not_3_out, or_1_out;
  wire [4:0] counter_1_q;

  not not_1 (not_1_out, icode[3]);
  not not_2 (not_2_out, icode[2]);
  not not_3 (not_3_out, icode[1]);
  and and_1 (and_1_out, not_1_out, icode[2], not_3_out, icode[0]);
  and and_2 (and_2_out, icode[3], not_2_out, icode[0]);
  or or_1 (or_1_out, and_1_out, and_2_out);
  Register #(.width(1)) register_1 (.D(or_1_out), .en(comparator_1_eq), .clk(clk), .Q(read));  // open: clr
  Comparator #(.width(5)) comparator_1 (.a(5'b01110), .b(counter_1_q), .eq(comparator_1_eq));  // open: gt, lt
  Counter_part #(.max('h1a), .width(5)) counter_1 (.clk(clk), .Q(counter_1_q));  // open: clr, load, up, count, D, carry
endmodule

module MemWrite (
  input  [3:0] icode,
  input  clk,
  output write
);

  wire and_1_out, and_2_out, comparator_1_eq, not_1_out, not_2_out, not_3_out, not_4_out, or_1_out;
  wire [4:0] counter_1_q;

  not not_1 (not_1_out, icode[3]);
  not not_2 (not_2_out, icode[2]);
  not not_3 (not_3_out, icode[1]);
  not not_4 (not_4_out, icode[0]);
  and and_1 (and_1_out, not_1_out, icode[2], not_3_out, not_4_out);
  and and_2 (and_2_out, icode[3], not_2_out, not_4_out);
  or or_1 (or_1_out, and_1_out, and_2_out);
  Register #(.width(1)) register_1 (.D(or_1_out), .en(comparator_1_eq), .clk(clk), .Q(write));  // open: clr
  Comparator #(.width(5)) comparator_1 (.a(5'b01110), .b(counter_1_q), .eq(comparator_1_eq));  // open: gt, lt
  Counter_part #(.max('h1a), .width(5)) counter_1 (.clk(clk), .Q(counter_1_q));  // open: clr, load, up, count, D, carry
endmodule

module MemAddress (
  input  [3:0] icode,
  input  clk,
  output out_3
);

  wire and_1_out, comparator_1_eq, not_1_out;
  wire [4:0] counter_1_q;

  not not_1 (not_1_out, icode[2]);
  and and_1 (and_1_out, icode[3], not_1_out, icode[0]);
  Register #(.width(1)) register_1 (.D(and_1_out), .en(comparator_1_eq), .clk(clk), .Q(out_3));  // open: clr
  Comparator #(.width(5)) comparator_1 (.a(5'b01110), .b(counter_1_q), .eq(comparator_1_eq));  // open: gt, lt
  Counter_part #(.max('h1a), .width(5)) counter_1 (.clk(clk), .Q(counter_1_q));  // open: clr, load, up, count, D, carry
endmodule

module MemData (
  input  [3:0] icode,
  input  clk,
  output out_3
);

  wire and_1_out, comparator_1_eq, not_1_out, not_2_out, not_3_out;
  wire [4:0] counter_1_q;

  not not_1 (not_1_out, icode[2]);
  not not_2 (not_2_out, icode[1]);
  not not_3 (not_3_out, icode[0]);
  and and_1 (and_1_out, icode[3], not_1_out, not_2_out, not_3_out);
  Register #(.width(1)) register_1 (.D(and_1_out), .en(comparator_1_eq), .clk(clk), .Q(out_3));  // open: clr
  Comparator #(.width(5)) comparator_1 (.a(5'b01110), .b(counter_1_q), .eq(comparator_1_eq));  // open: gt, lt
  Counter_part #(.max('h1a), .width(5)) counter_1 (.clk(clk), .Q(counter_1_q));  // open: clr, load, up, count, D, carry
endmodule

module IcodeToInstruction (
  input  i3,
  input  i2,
  input  i1,
  input  i0,
  output halt,
  output irmovq,
  output mrmovq,
  output jump,
  output rrmovq,
  output rmmovq,
  output opq,
  output pop,
  output push,
  output nop,
  output call,
  output ret
);

  wire not_1_out, not_2_out, not_3_out, not_4_out;

  not not_1 (not_1_out, i3);
  not not_2 (not_2_out, i2);
  not not_3 (not_3_out, i1);
  not not_4 (not_4_out, i0);
  and and_1 (halt, not_1_out, not_2_out, not_3_out, not_4_out);
  and and_2 (nop, not_1_out, not_2_out, not_3_out, i0);
  and and_3 (rrmovq, not_1_out, not_2_out, i1, not_4_out);
  and and_4 (irmovq, not_1_out, not_2_out, i1, i0);
  and and_5 (rmmovq, not_1_out, i2, not_3_out, not_4_out);
  and and_6 (mrmovq, not_1_out, i2, not_3_out, i0);
  and and_7 (opq, not_1_out, i2, i1, not_4_out);
  and and_8 (jump, not_1_out, i2, i1, i0);
  and and_9 (call, i3, not_2_out, not_3_out, not_4_out);
  and and_10 (ret, i3, not_2_out, not_3_out, i0);
  and and_11 (push, i3, not_2_out, i1, not_4_out);
  and and_12 (pop, i3, not_2_out, i1, i0);
endmodule

module Encoder (
  input  Halt,
  input  Irmovq,
  input  Mrmovq,
  input  Dest,
  input  Rrmovq,
  input  Rmmovq,
  input  Opq,
  input  Pushq,
  input  Popq,
  input  nop,
  input  call,
  input  ret,
  output [1:0] srcAMux,
  output [1:0] srcBMux
);

  wire oxf_out, oxff_out, ra_out, rb_out, rsp_out, rspp_out;

  or ra (ra_out, Rrmovq, Rmmovq, Opq, Pushq);
  or rsp (rsp_out, Popq, ret);
  or oxff (oxff_out, Halt, Irmovq, Rrmovq, Dest);
  or rb (rb_out, Rmmovq, Mrmovq, Opq);
  assign srcAMux = oxf_out ? 2'b00 : 2'bz;  // Controlled_Buffer controlled_buffer_1
  or oxf (oxf_out, Halt, Irmovq, Mrmovq, call, Dest);
  assign srcAMux = ra_out ? 2'b01 : 2'bz;  // Controlled_Buffer controlled_buffer_2
  assign srcAMux = rsp_out ? 2'b10 : 2'bz;  // Controlled_Buffer controlled_buffer_3
  or rspp (rspp_out, Popq, Pushq, call, ret);
  assign srcBMux = oxff_out ? 2'b00 : 2'bz;  // Controlled_Buffer controlled_buffer_4
  assign srcBMux = rb_out ? 2'b01 : 2'bz;  // Controlled_Buffer controlled_buffer_5
  assign srcBMux = rspp_out ? 2'b10 : 2'bz;  // Controlled_Buffer controlled_buffer_6
endmodule

module icodeToVal (
  input  i3,
  input  i2,
  input  i1,
  input  i0,
  output [1:0] srcAMux,
  output [1:0] srcBMux,
  output [1:0] dstEMux,
  output [1:0] dstMMux
);

  wire icodetoinstruction_1_call, icodetoinstruction_1_halt, icodetoinstruction_1_irmovq,
       icodetoinstruction_1_jump, icodetoinstruction_1_mrmovq, icodetoinstruction_1_opq,
       icodetoinstruction_1_pop, icodetoinstruction_1_push, icodetoinstruction_1_ret,
       icodetoinstruction_1_rmmovq, icodetoinstruction_1_rrmovq;

  IcodeToInstruction icodetoinstruction_1 (
    .i3(i3), .i2(i2), .i1(i1), .i0(i0), .halt(icodetoinstruction_1_halt),
    .irmovq(icodetoinstruction_1_irmovq), .mrmovq(icodetoinstruction_1_mrmovq),
    .jump(icodetoinstruction_1_jump), .rrmovq(icodetoinstruction_1_rrmovq),
    .rmmovq(icodetoinstruction_1_rmmovq), .opq(icodetoinstruction_1_opq), .pop(icodetoinstruction_1_pop),
    .push(icodetoinstruction_1_push), .call(icodetoinstruction_1_call), .ret(icodetoinstruction_1_ret));  // open: nop
  Encoder encoder_1 (
    .Halt(icodetoinstruction_1_halt), .Irmovq(icodetoinstruction_1_irmovq),
    .Mrmovq(icodetoinstruction_1_mrmovq), .Dest(icodetoinstruction_1_jump),
    .Rrmovq(icodetoinstruction_1_rrmovq), .Rmmovq(icodetoinstruction_1_rmmovq),
    .Opq(icodetoinstruction_1_opq), .Pushq(icodetoinstruction_1_push), .Popq(icodetoinstruction_1_pop),
    .call(icodetoinstruction_1_call), .ret(icodetoinstruction_1_ret), .srcAMux(srcAMux), .srcBMux(srcBMux));  // open: nop
  dst_encoder dst_encoder_1 (
    .halt(icodetoinstruction_1_halt), .rmmovq(icodetoinstruction_1_rmmovq),
    .jxxdest(icodetoinstruction_1_jump), .irmovq(icodetoinstruction_1_irmovq),
    .rrmovq(icodetoinstruction_1_rrmovq), .opq(icodetoinstruction_1_opq),
    .mrmovq(icodetoinstruction_1_mrmovq), .popq(icodetoinstruction_1_pop), .pushq(icodetoinstruction_1_push),
    .call(icodetoinstruction_1_call), .ret(icodetoinstruction_1_ret), .dstEMux(dstEMux), .dstMMux(dstMMux));  // open: nop
endmodule

module dst_encoder (
  input  halt,
  input  rmmovq,
  input  jxxdest,
  input  irmovq,
  input  rrmovq,
  input  opq,
  input  mrmovq,
  input  popq,
  input  pushq,
  input  nop,
  input  call,
  input  ret,
  output [1:0] dstEMux,
  output [1:0] dstMMux
);

  wire and_1_out, not_1_out, not_2_out, oxf_out, rb_out, rsp_out;

  not not_1 (not_1_out, mrmovq);
  not not_2 (not_2_out, popq);
  or oxf (oxf_out, halt, rmmovq, mrmovq, jxxdest);
  or rb (rb_out, irmovq, rrmovq, opq);
  or rsp (rsp_out, pushq, popq, ret, call);
  and and_1 (and_1_out, not_1_out, not_2_out);
  assign dstEMux = oxf_out ? 2'b00 : 2'bz;  // Controlled_Buffer controlled_buffer_1
  assign dstEMux = rb_out ? 2'b01 : 2'bz;  // Controlled_Buffer controlled_buffer_2
  assign dstEMux = rsp_out ? 2'b11 : 2'bz;  // Controlled_Buffer controlled_buffer_3
  assign dstMMux = and_1_out ? 2'b00 : 2'bz;  // Controlled_Buffer controlled_buffer_4
  assign dstMMux = mrmovq ? 2'b10 : 2'bz;  // Controlled_Buffer controlled_buffer_5
  assign dstMMux = popq ? 2'b10 : 2'bz;  // Controlled_Buffer controlled_buffer_6
endmodule

module icodeToInputVals (
  input  [3:0] rA,
  input  [3:0] rB,
  input  [3:0] rsp,
  input  i0,
  input  i1,
  input  i2,
  input  i3,
  output [3:0] srcA,
  output [3:0] srcB,
  output [3:0] dstE,
  output [3:0] dstM
);

  wire [1:0] icodetoval_1_dstemux, icodetoval_1_dstmmux, icodetoval_1_srcamux, icodetoval_1_srcbmux;

  icodeToVal icodetoval_1 (
    .i3(i3), .i2(i2), .i1(i1), .i0(i0), .srcAMux(icodetoval_1_srcamux), .srcBMux(icodetoval_1_srcbmux),
    .dstEMux(icodetoval_1_dstemux), .dstMMux(icodetoval_1_dstmmux));
  Multiplexer #(.select(2), .width(4)) multiplexer_1 (
    .in0(4'b1111), .in1(rA), .in2(rsp), .out(srcA), .sel(icodetoval_1_srcamux));  // open: in3
  Multiplexer #(.select(2), .width(4)) multiplexer_2 (
    .in0(4'b1111), .in1(rB), .in2(rsp), .out(srcB), .sel(icodetoval_1_srcbmux));  // open: in3
  Multiplexer #(.select(2), .width(4)) multiplexer_3 (
    .in0(4'b1111), .in1(rB), .in2(rA), .in3(rsp), .out(dstE), .sel(icodetoval_1_dstemux));
  Multiplexer #(.select(2), .width(4)) multiplexer_4 (
    .in0(4'b1111), .in1(rB), .in2(rA), .in3(rsp), .out(dstM), .sel(icodetoval_1_dstmmux));
endmodule

module addr_decode (
  input  [3:0] src,
  output r0,
  output r1,
  output r2,
  output r3,
  output r4,
  output r5,
  output r6,
  output r7,
  output r8,
  output r9,
  output r10,
  output r11,
  output r12,
  output r13,
  output r14
);

  wire not_1_out, not_2_out, not_3_out, not_4_out;

  not not_1 (not_1_out, src[3]);
  not not_2 (not_2_out, src[2]);
  not not_3 (not_3_out, src[1]);
  not not_4 (not_4_out, src[0]);
  and and_1 (r0, not_1_out, not_2_out, not_3_out, not_4_out);
  and and_2 (r1, not_1_out, not_2_out, not_3_out, src[0]);
  and and_3 (r2, not_1_out, not_2_out, src[1], not_4_out);
  and and_4 (r3, not_1_out, not_2_out, src[1], src[0]);
  and and_5 (r4, not_1_out, src[2], not_3_out, not_4_out);
  and and_6 (r5, not_1_out, src[2], not_3_out, src[0]);
  and and_7 (r6, not_1_out, src[2], src[1], not_4_out);
  and and_8 (r7, not_1_out, src[2], src[1], src[0]);
  and and_9 (r8, src[3], not_2_out, not_3_out, not_4_out);
  and and_10 (r9, src[3], not_2_out, not_3_out, src[0]);
  and and_11 (r10, src[3], not_2_out, src[1], not_4_out);
  and and_12 (r11, src[3], not_2_out, src[1], src[0]);
  and and_13 (r12, src[3], src[2], not_3_out, not_4_out);
  and and_14 (r13, src[3], src[2], not_3_out, src[0]);
  and and_15 (r14, src[3], src[2], src[1], not_4_out);
endmodule

module MemCounter (
  input  i0,
  input  i1,
  input  i2,
  input  i3,
  output b0,
  output b1,
  output b2,
  output b3,
  output b4,
  output b5,
  output b6,
  output b7,
  output b8
);

  wire not_1_out, not_2_out, not_3_out, not_4_out;

  not not_1 (not_1_out, i0);
  not not_2 (not_2_out, i1);
  not not_3 (not_3_out, i2);
  not not_4 (not_4_out, i3);
  and and_1 (b0, not_1_out, not_2_out, not_3_out, not_4_out);
  and and_2 (b1, not_1_out, not_2_out, not_3_out, i3);
  and and_3 (b2, not_1_out, not_2_out, i2, not_4_out);
  and and_4 (b3, not_1_out, not_2_out, i2, i3);
  and and_5 (b4, not_1_out, i1, not_3_out, not_4_out);
  and and_6 (b5, not_1_out, i1, not_3_out, i3);
  and and_7 (b6, not_1_out, i1, i2, not_4_out);
  and and_8 (b7, not_1_out, i1, i2, i3);
  and and_9 (b8, i0, not_2_out, not_3_out, not_4_out);
endmodule

module stat (
  input  [3:0] halt,
  input  imem,
  input  instr_valid,
  input  dmem,
  input  clk,
  output out_6
);

  wire and_1_out, comparator_1_eq, decoder_1_out0, register_1_q, undriven;
  wire [4:0] counter_1_q;

  Decoder #(.select(4)) decoder_1 (
    .out0(decoder_1_out0), .sel(halt));  // open: out1, out2, out3, out4, out5, out6, out7, out8, out9, out10, out11, out12, out13, out14, out15, en
  Counter_part #(.max('h1a), .width(5)) counter_1 (.clk(clk), .Q(counter_1_q));  // open: clr, load, up, count, D, carry
  Register #(.width(1)) register_1 (.D(decoder_1_out0), .clk(clk), .Q(register_1_q));  // open: en, clr
  Multiplexer multiplexer_1 (.in0(1'b1), .in1(1'b0), .out(out_6), .sel(and_1_out));
  and and_1 (and_1_out, register_1_q, comparator_1_eq);
  Comparator #(.width(5)) comparator_1 (.a(5'b01011), .b(counter_1_q), .eq(comparator_1_eq));  // open: gt, lt
  // OR_Gate or_1 has open pins: in0=undriven, in1=imem, in2=instr_valid, in3=dmem, out=open
endmodule

module decmux (
  input  wen,
  input  counter,
  output enable
);

  Multiplexer multiplexer_1 (.in0(1'b0), .in1(wen), .out(enable), .sel(counter));
endmodule
